# Fritzing sketch MinimalPiClock (saved by Fritzing 0.9.3b)
circuit board: 16cm x 10cm
breadboards: 1

parts:
  VCC1 = 4 x AAA Battery Mount
  C2 = Capacitor [package=cap-pth-small2]
  C1 = Capacitor [package=cap-pth-small2]
  Y1 = CRYSTAL [package=crystal-smd-10.5x4.8-2pin]
  BEEP = Piezo Speaker
  J5V = female pin header, 2 pins [form="♀ (female)"]
  A2 = atmega328 [package=dip]

nets:
  N1: VCC1.-, C2.2, C1.2, BEEP.pin1, J5V.pin1, A2.GND
  N2: VCC1.+, J5V.pin2, A2.VCC, A2.AVCC, A2.AREF
  N3: C2.1, Y1.2, A2.XLAT2
  N4: C1.1, Y1.1, A2.XLAT1
  N5: BEEP.pin2, A2.D8

notes:
  Capacitors: 22 pF
  Crystal: 16 MHz
  If this pin (A0) is connected to GND,
  at startup the piezo
  will buzz
