# Fritzing sketch minimal_pi_clock (saved by Fritzing 1.0.1rc)
circuit board: 16cm x 10cm
breadboards: 1

parts:
  X2 = USB Connectors [package=usb-b-smt]
  BEEP1 = Piezo Speaker
  A3 = atmega328 [package=dip]
  C3 = Capacitor [package=cap-pth-small2]
  Y2 = CRYSTAL [package=crystal-smd-10.5x4.8-2pin]
  C4 = Capacitor [package=cap-pth-small2]

nets:
  GND: X2.GND, BEEP1.pin1, A3.GND, C3.2, C4.2
  N1: X2.VBUS, A3.VCC, A3.AVCC, A3.AREF
  N2: BEEP1.pin2, A3.D8
  N3: A3.XLAT1, Y2.2, C4.1
  N4: A3.XLAT2, C3.1, Y2.1

notes:
  5 volt in any way
  Capacitors: 22 pF
  Crystal: 16 MHz
